// Logisim project _SIMP.circ as structural Verilog: 7 circuits, main circuit main
module main (
  input  [7:0] I,
  input  start,
  output [7:0] O
);

  wire clock_1_out, uck_1_ck_out, uck_1_led_out, ucm_1_read_out, ucm_1_write_out, ucp_1_end_out;
  wire [4:0] ual_1_copnz_out;
  wire [7:0] ram_1_dout, rom_1_data, ual_1_r1_out, ual_1_r2_out, ucp_1_high_adress_out, ucp_1_low_adress_out,
       ucp_1_ram_out;
  wire [15:0] ucp_1_cpc_out;

  LED led_1 (.in(uck_1_led_out));
  Clock clock_1 (.out(clock_1_out));
  UCK uck_1 (
    .CK_out(uck_1_ck_out), .LED_out(uck_1_led_out), .CK_in(clock_1_out), .start_in(start),
    .end_in(ucp_1_end_out));
  RAM #(.addrWidth(16)) ram_1 (
    .addr({ucp_1_high_adress_out, ucp_1_low_adress_out}), .we(ucm_1_write_out), .oe(ucm_1_read_out),
    .clk(uck_1_ck_out), .din(ucp_1_ram_out), .dout(ram_1_dout));
  UCM ucm_1 (.write_out(ucm_1_write_out), .read_out(ucm_1_read_out), .instruction(rom_1_data));
  UCP ucp_1 (
    .ram_out(ucp_1_ram_out), .CPC_out(ucp_1_cpc_out[7:0]), .CPA_out(ucp_1_cpc_out[15:8]),
    .high_adress_out(ucp_1_high_adress_out), .low_adress_out(ucp_1_low_adress_out), .end_out(ucp_1_end_out),
    .CK(uck_1_ck_out), .r2_in(ual_1_r2_out), .ram_in(ram_1_dout), .r1_in(ual_1_r1_out),
    .instruction(rom_1_data), .COPNZ_in(ual_1_copnz_out));
  ROM #(.addrWidth(16)) rom_1 (.addr(ucp_1_cpc_out), .data(rom_1_data));
  UAL ual_1 (
    .OUT_out(O), .COPNZ_out(ual_1_copnz_out), .r1_out(ual_1_r1_out), .r2_out(ual_1_r2_out),
    .CK(uck_1_ck_out), .ram_in(ram_1_dout), .IN_in(I), .instruction(rom_1_data));

  // Notes on the sheet:
  //   contents of rom_1 (hex, n*v repeats v):
  //   14 1
endmodule

module UAL (
  input  [7:0] instruction,
  input  CK,
  input  [7:0] ram_in,
  input  [7:0] IN_in,
  output [7:0] r2_out,
  output [7:0] r1_out,
  output [7:0] OUT_out,
  output [4:0] COPNZ_out
);

  wire add_out, and_1_out, and_2_out, and_3_out, and_4_out, and_5_out, and_6_out, and_7_out, and_8_out,
       and_9_out, and_10_out, and_11_out, and_12_out, and_13_out, and_14_out, and_15_out, and_16_out,
       and_17_out, and_18_out, and_19_out, and_20_out, and_21_out, and_22_out, and_23_out, and_24_out,
       and_25_out, and_26_out, AU_carry_out, hi_lo_V_out, iget_out, leq_out, les_leq_out, mget_out,
       nand0_out, nand_1_out, nand_2_out, nand_3_out, nand_4_out, nand_5_out, nand_6_out, nand_7_out,
       nand_8_out, nand_9_out, nand_10_out, nand_11_out, nand_14_out, nand_15_out, nand_16_out, nand_18_out,
       nand_19_out, nand_20_out, nand_23_out, nand_25_out, nand_26_out, nand_27_out, nand_28_out,
       nand_30_out, nand_31_out, nand_32_out, nand_34_out, nand_37_out, nand_38_out, nand_39_out,
       nand_40_out, nand_41_out, nand_43_out, nand_44_out, nand_45_out, nand_46_out, nand_47_out,
       nand_48_out, nand_49_out, nand_50_out, nand_51_out, or0_out, or_9_out, or_10_out, or_11_out,
       or_12_out, or_13_out, or_14_out, or_15_out, or_16_out, or_17_out, or_18_out, pop_r_out, set_A_out,
       set_B_out, set_out, set_V_out, set_X_out, shift_rot_carry_out, shift_rot_out, sub_out, xor0_out,
       xor_4_out, xor_5_out, xor_6_out, xor_8_out, xor_12_out, xor_15_out, xor_16_out, xor_17_out,
       xor_20_out, xor_24_out, xor_25_out, xor_27_out, xor_29_out, xor_30_out, xor_32_out, xor_33_out;
  wire [0:0] nand_36_out;
  wire [4:0] Z_out;
  wire [7:0] B_AU_A_shift_rot_x, B_else_A_NAND_x, B_else_A_OR_x, B_else_A_XOR_x, B_left_A_right_x,
       B_loV_A_hiV_x, B_op_A_comp_x, B_q, B_ram_A_hi_lo_V_x, B_ram_A_IN_x, B_ram_A_math_x, nand_33_out,
       or_8_out, r1_B_A_A_B_x, r1_B_V_A_X_x, r2_B_A_A_B_x, r2_B_V_A_X_x, V_q, X_q, xor_26_out, xor_31_out;
  wire [7:7] N_out, nand_35_out;

  nand nand_1 (nand_1_out, instruction[2], r2_out[0]);
  nand shift_rot_carry (shift_rot_carry_out, nand_1_out, nand_4_out);
  nand nand_2 (nand_2_out, shift_rot_out, shift_rot_carry_out);
  nand AU_carry (AU_carry_out, nand_7_out, nand_8_out);
  xor xor_1 (Z_out[3], AU_carry_out, nand_9_out);
  nand nand_3 (nand_3_out, instruction[2], instruction[2]);
  nand nand_4 (nand_4_out, nand_3_out, r2_out[7]);
  nand nand_5 (nand_5_out, shift_rot_out, shift_rot_out);
  nand nand_6 (nand_6_out, nand_5_out, AU_carry_out);
  nand carry_MUX (Z_out[4], nand_2_out, nand_6_out);
  nand nand_7 (nand_7_out, r2_out[7], xor_4_out);
  nand nand_8 (nand_8_out, nand_9_out, xor_5_out);
  xor xor_2 (xor_31_out[7], xor_5_out, nand_9_out);
  nand nand_9 (nand_9_out, nand_11_out, nand_10_out);
  nand nand_10 (nand_10_out, nand_14_out, xor_6_out);
  xor xor_3 (xor_31_out[6], xor_6_out, nand_14_out);
  or or_1 (or_8_out[7], r2_out[7], r1_out[7]);
  xor xor_4 (xor_4_out, r1_out[7], sub_out);
  xor xor_5 (xor_5_out, r2_out[7], xor_4_out);
  nand nand_11 (nand_11_out, r2_out[6], xor_8_out);
  xor xor_6 (xor_6_out, r2_out[6], xor_8_out);
  nand nand_12 (nand_33_out[7], r2_out[7], r1_out[7]);
  or or_2 (or_8_out[6], r2_out[6], r1_out[6]);
  xor xor_7 (xor_26_out[7], r2_out[7], r1_out[7]);
  xor xor_8 (xor_8_out, r1_out[6], sub_out);
  nand nand_13 (nand_33_out[6], r2_out[6], r1_out[6]);
  or or_3 (or_8_out[5], r2_out[5], r1_out[5]);
  xor xor_9 (xor_26_out[6], r2_out[6], r1_out[6]);
  nand nand_14 (nand_14_out, nand_18_out, nand_15_out);
  nand nand_15 (nand_15_out, nand_16_out, xor_12_out);
  xor xor_10 (xor_31_out[5], xor_12_out, nand_16_out);
  nand nand_16 (nand_16_out, nand_19_out, nand_20_out);
  nand nand_17 (nand_33_out[5], r2_out[5], r1_out[5]);
  or or_4 (or_8_out[4], r2_out[4], r1_out[4]);
  xor xor_11 (xor_26_out[5], r2_out[5], r1_out[5]);
  nand nand_18 (nand_18_out, r2_out[5], xor_15_out);
  xor xor_12 (xor_12_out, r2_out[5], xor_15_out);
  nand nand_19 (nand_19_out, r2_out[4], xor_16_out);
  nand nand_20 (nand_20_out, nand_23_out, xor_17_out);
  xor xor_13 (xor_31_out[4], xor_17_out, nand_23_out);
  nand nand_21 (nand_33_out[4], r2_out[4], r1_out[4]);
  or or_5 (or_8_out[3], r2_out[3], r1_out[3]);
  xor xor_14 (xor_26_out[4], r2_out[4], r1_out[4]);
  xor xor_15 (xor_15_out, r1_out[5], sub_out);
  xor xor_16 (xor_16_out, r1_out[4], sub_out);
  xor xor_17 (xor_17_out, r2_out[4], xor_16_out);
  nand nand_22 (nand_33_out[3], r2_out[3], r1_out[3]);
  or or_6 (or_8_out[2], r2_out[2], r1_out[2]);
  xor xor_18 (xor_26_out[3], r2_out[3], r1_out[3]);
  nand nand_23 (nand_23_out, nand_25_out, nand_26_out);
  nand nand_24 (nand_33_out[2], r2_out[2], r1_out[2]);
  or or_7 (or_8_out[1], r2_out[1], r1_out[1]);
  xor xor_19 (xor_26_out[2], r2_out[2], r1_out[2]);
  nand nand_25 (nand_25_out, r2_out[3], xor_24_out);
  nand nand_26 (nand_26_out, nand_27_out, xor_20_out);
  xor xor_20 (xor_20_out, r2_out[3], xor_24_out);
  xor xor_21 (xor_31_out[3], xor_20_out, nand_27_out);
  nand nand_27 (nand_27_out, nand_30_out, nand_28_out);
  nand nand_28 (nand_28_out, nand_34_out, xor_25_out);
  xor xor_22 (xor_31_out[2], xor_25_out, nand_34_out);
  nand nand_29 (nand_33_out[1], r2_out[1], r1_out[1]);
  or or_8 (or_8_out[0], r2_out[0], r1_out[0]);
  xor xor_23 (xor_26_out[1], r2_out[1], r1_out[1]);
  xor xor_24 (xor_24_out, r1_out[3], sub_out);
  nand nand_30 (nand_30_out, r2_out[2], xor_27_out);
  xor xor_25 (xor_25_out, r2_out[2], xor_27_out);
  nand nand_31 (nand_31_out, r2_out[0], instruction[3]);
  nand nand_32 (nand_32_out, instruction[3], r2_out[7]);
  nand nand_33 (nand_33_out[0], r2_out[0], r1_out[0]);
  xor xor_26 (xor_26_out[0], r2_out[0], r1_out[0]);
  nand nand_34 (nand_34_out, nand_39_out, nand_37_out);
  xor xor_27 (xor_27_out, r1_out[2], sub_out);
  nand nand_35 (nand_35_out[7], nand_31_out, nand_31_out);
  nand nand_36 (nand_36_out[0], nand_32_out, nand_32_out);
  nand nand_37 (nand_37_out, nand_38_out, xor_29_out);
  xor xor_28 (xor_31_out[1], xor_29_out, nand_38_out);
  nand nand_38 (nand_38_out, nand_40_out, nand_41_out);
  MUX_8_bits B_left_A_right (
    .X(B_left_A_right_x), .B({r2_out[6:0], nand_36_out[0]}), .A({nand_35_out[7], r2_out[7:1]}),
    .Sel(instruction[2]));
  MUX_8_bits B_AU_A_shift_rot (.X(B_AU_A_shift_rot_x), .B(xor_31_out), .A(B_left_A_right_x), .Sel(shift_rot_out));
  MUX_8_bits B_else_A_NAND (.X(B_else_A_NAND_x), .B(B_AU_A_shift_rot_x), .A(nand_33_out), .Sel(nand0_out));
  MUX_8_bits B_else_A_OR (.X(B_else_A_OR_x), .B(B_else_A_NAND_x), .A(or_8_out), .Sel(or0_out));
  MUX_8_bits B_else_A_XOR (.X(B_else_A_XOR_x), .B(B_else_A_OR_x), .A(xor_26_out), .Sel(xor0_out));
  nand nand_39 (nand_39_out, r2_out[1], xor_32_out);
  xor xor_29 (xor_29_out, r2_out[1], xor_32_out);
  nand nand_40 (nand_40_out, r2_out[0], xor_33_out);
  nand nand_41 (nand_41_out, sub_out, xor_30_out);
  xor xor_30 (xor_30_out, r2_out[0], xor_33_out);
  xor xor_31 (xor_31_out[0], xor_30_out, sub_out);
  xor xor_32 (xor_32_out, r1_out[1], sub_out);
  xor xor_33 (xor_33_out, r1_out[0], sub_out);
  MUX_8_bits r2_A_V_X_B_A_B (.X(r2_out), .B(r2_B_A_A_B_x), .A(r2_B_V_A_X_x), .Sel(instruction[1]));
  MUX_8_bits r1_A_V_X_B_A_B (.X(r1_out), .B(r1_B_A_A_B_x), .A(r1_B_V_A_X_x), .Sel(instruction[3]));
  nand sub (sub_out, add_out, add_out);
  or or_9 (or_9_out, B_else_A_XOR_x[7], B_else_A_XOR_x[6]);
  or or_10 (or_10_out, B_else_A_XOR_x[5], B_else_A_XOR_x[4]);
  or or_11 (or_11_out, B_else_A_XOR_x[3], B_else_A_XOR_x[2]);
  or or_12 (or_12_out, B_else_A_XOR_x[1], B_else_A_XOR_x[0]);
  MUX_8_bits r2_B_V_A_X (.X(r2_B_V_A_X_x), .B(V_q), .A(X_q), .Sel(instruction[0]));
  MUX_8_bits r1_B_V_A_X (.X(r1_B_V_A_X_x), .B(V_q), .A(X_q), .Sel(instruction[2]));
  nand nand_42 (Z_out[2], B_else_A_XOR_x[0], B_else_A_XOR_x[0]);
  or or_13 (or_13_out, or_9_out, or_10_out);
  or or_14 (or_14_out, or_13_out, or_15_out);
  or or_15 (or_15_out, or_11_out, or_12_out);
  MUX_8_bits B_op_A_comp (.X(B_op_A_comp_x), .B(B_else_A_XOR_x), .A({8{N_out[7]}}), .Sel(les_leq_out));
  Register A (.D(B_ram_A_IN_x), .en(or_16_out), .clk(CK), .Q(OUT_out));  // open: clr
  MUX_8_bits B_ram_A_IN (.X(B_ram_A_IN_x), .B(ram_in), .A(IN_in), .Sel(iget_out));
  Register V (.D(B_ram_A_hi_lo_V_x), .en(or_17_out), .clk(CK), .Q(V_q));  // open: clr
  MUX_8_bits B_ram_A_math (.X(B_ram_A_math_x), .B(ram_in), .A(B_op_A_comp_x), .Sel(instruction[7]));
  MUX_8_bits r2_B_A_A_B (.X(r2_B_A_A_B_x), .B(OUT_out), .A(B_q), .Sel(instruction[0]));
  MUX_8_bits r1_B_A_A_B (.X(r1_B_A_A_B_x), .B(OUT_out), .A(B_q), .Sel(instruction[2]));
  nand nand_43 (nand_43_out, Z_out[0], leq_out);
  nand Z (Z_out[0], or_14_out, or_14_out);
  Register B (.D(ram_in), .en(set_B_out), .clk(CK), .Q(B_q));  // open: clr
  Register X (.D(B_ram_A_math_x), .en(or_18_out), .clk(CK), .Q(X_q));  // open: clr
  nand nand_44 (nand_44_out, nand_43_out, nand_43_out);
  or N (N_out[7], nand_44_out, B_else_A_XOR_x[7]);
  or or_16 (or_16_out, set_A_out, iget_out);
  or or_17 (or_17_out, set_V_out, hi_lo_V_out);
  or or_18 (or_18_out, set_X_out, instruction[7]);
  MUX_8_bits B_ram_A_hi_lo_V (.X(B_ram_A_hi_lo_V_x), .B(ram_in), .A(B_loV_A_hiV_x), .Sel(hi_lo_V_out));
  MUX_8_bits B_loV_A_hiV (
    .X(B_loV_A_hiV_x), .B({instruction[3:0], V_q[3:0]}), .A({V_q[7:4], instruction[3:0]}),
    .Sel(instruction[4]));
  Register #(.width(5)) COPNZ (
    .D({Z_out[4:2], N_out[7], Z_out[0]}), .en(instruction[7]), .clk(CK), .Q(COPNZ_out));  // open: clr
  and set_A (set_A_out, and_18_out, set_out);
  and set_B (set_B_out, and_19_out, set_out);
  and set_V (set_V_out, and_20_out, set_out);
  and set_X (set_X_out, and_21_out, set_out);
  or set (set_out, pop_r_out, mget_out);
  and pop_r (pop_r_out, and_1_out, and_2_out);
  and shift_rot (shift_rot_out, and_3_out, and_4_out);
  and nand0 (nand0_out, and_5_out, and_6_out);
  and or0 (or0_out, and_7_out, and_8_out);
  and xor0 (xor0_out, and_9_out, and_10_out);
  and leq (leq_out, and_11_out, and_12_out);
  and add (add_out, and_13_out, and_14_out);
  and les_leq (les_leq_out, and_15_out, instruction[5]);
  and iget (iget_out, and_16_out, and_17_out);
  and mget (mget_out, and_22_out, and_23_out);
  and and_1 (and_1_out, and_24_out, and_25_out);
  and and_2 (and_2_out, instruction[3], nand_51_out);
  and hi_lo_V (hi_lo_V_out, and_26_out, instruction[5]);
  and and_3 (and_3_out, instruction[7], nand_47_out);
  and and_4 (and_4_out, instruction[5], nand_45_out);
  and and_5 (and_5_out, instruction[7], nand_47_out);
  and and_6 (and_6_out, instruction[5], instruction[4]);
  and and_7 (and_7_out, instruction[7], instruction[6]);
  and and_8 (and_8_out, nand_46_out, nand_45_out);
  and and_9 (and_9_out, instruction[7], instruction[6]);
  and and_10 (and_10_out, nand_46_out, instruction[4]);
  and and_11 (and_11_out, instruction[7], instruction[6]);
  and and_12 (and_12_out, instruction[5], instruction[4]);
  and and_13 (and_13_out, instruction[7], nand_47_out);
  and and_14 (and_14_out, nand_46_out, nand_45_out);
  and and_15 (and_15_out, instruction[7], instruction[6]);
  and and_16 (and_16_out, nand_48_out, instruction[6]);
  and and_17 (and_17_out, nand_46_out, nand_45_out);
  and and_18 (and_18_out, nand_50_out, nand_49_out);
  and and_19 (and_19_out, nand_50_out, instruction[0]);
  and and_20 (and_20_out, instruction[1], nand_49_out);
  and and_21 (and_21_out, instruction[1], instruction[0]);
  and and_22 (and_22_out, nand_48_out, nand_47_out);
  and and_23 (and_23_out, instruction[5], nand_45_out);
  and and_24 (and_24_out, nand_48_out, nand_47_out);
  and and_25 (and_25_out, nand_46_out, instruction[4]);
  and and_26 (and_26_out, nand_48_out, instruction[6]);
  nand nand_45 (nand_45_out, instruction[4], instruction[4]);
  nand nand_46 (nand_46_out, instruction[5], instruction[5]);
  nand nand_47 (nand_47_out, instruction[6], instruction[6]);
  nand nand_48 (nand_48_out, instruction[7], instruction[7]);
  nand nand_49 (nand_49_out, instruction[0], instruction[0]);
  nand nand_50 (nand_50_out, instruction[1], instruction[1]);
  nand nand_51 (nand_51_out, instruction[2], instruction[2]);
endmodule

module UCP (
  input  [7:0] instruction,
  input  [7:0] r1_in,
  input  [7:0] r2_in,
  input  CK,
  input  [4:0] COPNZ_in,
  input  [7:0] ram_in,
  output [7:0] low_adress_out,
  output [7:0] ram_out,
  output end_out,
  output [7:0] high_adress_out,
  output [7:0] CPC_out,
  output [7:0] CPA_out
);

  wire and_2_out, and_3_out, and_4_out, and_5_out, and_6_out, and_7_out, and_9_out, and_10_out, and_11_out,
       and_12_out, and_13_out, and_14_out, and_15_out, and_16_out, and_17_out, and_18_out, and_19_out,
       and_20_out, and_21_out, and_22_out, and_23_out, and_24_out, and_25_out, and_26_out, and_27_out,
       and_28_out, and_29_out, and_30_out, and_31_out, and_32_out, and_33_out, and_34_out, and_35_out,
       and_36_out, and_37_out, and_38_out, and_39_out, and_40_out, and_41_out, and_42_out, and_43_out,
       and_44_out, and_45_out, and_46_out, and_47_out, and_48_out, and_49_out, and_50_out, and_51_out,
       and_52_out, and_53_out, and_54_out, and_55_out, and_56_out, and_57_out, and_58_out, and_59_out, C_out,
       E_out, F_out, jmp_out, N_out, nand_4_out, nand_5_out, nand_6_out, nand_7_out, nand_8_out, nand_9_out,
       nand_10_out, nand_11_out, O_out, or_1_out, or_2_out, or_3_out, or_4_out, or_5_out, or_6_out, or_7_out,
       or_8_out, or_9_out, or_10_out, or_11_out, or_12_out, or_13_out, or_14_out, P_out, pop_s_out,
       push_s_out, stack_out, true_out, xor_4_out, xor_8_out, xor_14_out, xor_18_out, xor_22_out, xor_26_out,
       xor_29_out, xor_30_out, xor_31_out, xor_32_out, xor_33_out, xor_34_out, xor_35_out, xor_36_out, Z_out;
  wire [1:0] EF_q, nand_1_out;
  wire [7:0] B_CPA_A_JPA_x, B_CPC_A_CPA_x, B_CPC_A_JPC_x, B_pop_A_push_x, B_SP_A_MPA_x, B_SP_A_ram_x,
       B_SP_MPA_A_CPC_CPA_x, JPA_q, JPC_q, nand_2_out, nand_3_out, SP_q, xor_27_out;

  or or_1 (or_1_out, or_3_out, or_6_out);
  and and_1 (nand_1_out[1], and_3_out, and_6_out);
  or or_2 (or_2_out, B_SP_A_ram_x[0], B_SP_A_ram_x[1]);
  or or_3 (or_3_out, or_2_out, or_4_out);
  or or_4 (or_4_out, B_SP_A_ram_x[2], B_SP_A_ram_x[3]);
  or or_5 (or_5_out, B_SP_A_ram_x[4], B_SP_A_ram_x[5]);
  or or_6 (or_6_out, or_5_out, or_7_out);
  or or_7 (or_7_out, B_SP_A_ram_x[6], B_SP_A_ram_x[7]);
  and and_2 (and_2_out, B_SP_A_ram_x[0], B_SP_A_ram_x[1]);
  and and_3 (and_3_out, and_2_out, and_4_out);
  and and_4 (and_4_out, B_SP_A_ram_x[2], B_SP_A_ram_x[3]);
  and and_5 (and_5_out, B_SP_A_ram_x[4], B_SP_A_ram_x[5]);
  and and_6 (and_6_out, and_5_out, and_7_out);
  and and_7 (and_7_out, B_SP_A_ram_x[6], B_SP_A_ram_x[7]);
  nand nand_1 (nand_1_out[0], or_1_out, or_1_out);
  MUX_8_bits B_CPA_A_JPA (.X(B_CPA_A_JPA_x), .B(xor_27_out), .A(JPA_q), .Sel(and_33_out));
  MUX_8_bits B_CPC_A_JPC (.X(B_CPC_A_JPC_x), .B(nand_2_out), .A(JPC_q), .Sel(and_33_out));
  Register SP (.D(B_SP_A_ram_x), .en(stack_out), .clk(CK), .Q(SP_q));  // open: clr
  Register CPA (.D(B_CPA_A_JPA_x), .en(1'b1), .clk(CK), .Q(CPA_out));  // open: clr
  Register CPC (.D(B_CPC_A_JPC_x), .en(1'b1), .clk(CK), .Q(CPC_out));  // open: clr
  MUX_8_bits B_SP_A_ram (.X(B_SP_A_ram_x), .B(nand_3_out), .A(ram_in), .Sel(and_29_out));
  and and_8 (end_out, CPA_out[7], and_11_out);
  and and_9 (and_9_out, CPC_out[7], and_12_out);
  and and_10 (and_10_out, xor_4_out, and_15_out);
  xor xor_1 (nand_3_out[7], SP_q[7], and_10_out);
  and and_11 (and_11_out, CPA_out[6], and_13_out);
  xor xor_2 (xor_27_out[7], CPA_out[7], and_11_out);
  and and_12 (and_12_out, CPC_out[6], and_14_out);
  xor xor_3 (nand_2_out[7], CPC_out[7], and_12_out);
  xor xor_4 (xor_4_out, instruction[3], SP_q[6]);
  xor xor_5 (nand_3_out[6], SP_q[6], and_15_out);
  and and_13 (and_13_out, CPA_out[5], and_17_out);
  xor xor_6 (xor_27_out[6], CPA_out[6], and_13_out);
  and and_14 (and_14_out, CPC_out[5], and_18_out);
  xor xor_7 (nand_2_out[6], CPC_out[6], and_14_out);
  xor xor_8 (xor_8_out, instruction[3], SP_q[5]);
  and and_15 (and_15_out, xor_8_out, and_16_out);
  xor xor_9 (xor_27_out[5], CPA_out[5], and_17_out);
  xor xor_10 (nand_2_out[5], CPC_out[5], and_18_out);
  and and_16 (and_16_out, xor_14_out, and_21_out);
  xor xor_11 (nand_3_out[5], SP_q[5], and_16_out);
  and and_17 (and_17_out, CPA_out[4], and_19_out);
  xor xor_12 (xor_27_out[4], CPA_out[4], and_19_out);
  and and_18 (and_18_out, CPC_out[4], and_20_out);
  xor xor_13 (nand_2_out[4], CPC_out[4], and_20_out);
  xor xor_14 (xor_14_out, instruction[3], SP_q[4]);
  xor xor_15 (nand_3_out[4], SP_q[4], and_21_out);
  and and_19 (and_19_out, CPA_out[3], and_22_out);
  xor xor_16 (xor_27_out[3], CPA_out[3], and_22_out);
  and and_20 (and_20_out, CPC_out[3], and_23_out);
  xor xor_17 (nand_2_out[3], CPC_out[3], and_23_out);
  xor xor_18 (xor_18_out, instruction[3], SP_q[3]);
  and and_21 (and_21_out, xor_18_out, and_24_out);
  and and_22 (and_22_out, CPA_out[2], and_25_out);
  and and_23 (and_23_out, CPC_out[2], and_26_out);
  and and_24 (and_24_out, xor_22_out, and_28_out);
  xor xor_19 (nand_3_out[3], SP_q[3], and_24_out);
  and and_25 (and_25_out, CPA_out[1], and_27_out);
  xor xor_20 (xor_27_out[2], CPA_out[2], and_25_out);
  and and_26 (and_26_out, CPC_out[1], CPC_out[0]);
  xor xor_21 (nand_2_out[2], CPC_out[2], and_26_out);
  xor xor_22 (xor_22_out, instruction[3], SP_q[2]);
  xor xor_23 (nand_3_out[2], SP_q[2], and_28_out);
  and and_27 (and_27_out, CPA_out[0], and_9_out);
  xor xor_24 (xor_27_out[1], CPA_out[1], and_27_out);
  xor xor_25 (nand_2_out[1], CPC_out[1], CPC_out[0]);
  xor xor_26 (xor_26_out, instruction[3], SP_q[1]);
  and and_28 (and_28_out, xor_26_out, xor_29_out);
  xor xor_27 (xor_27_out[0], CPA_out[0], and_9_out);
  nand nand_2 (nand_2_out[0], CPC_out[0], CPC_out[0]);
  xor xor_28 (nand_3_out[1], SP_q[1], xor_29_out);
  Register JPA (.D(ram_in), .en(and_32_out), .clk(CK), .Q(JPA_q));  // open: clr
  Register MPA (.D(ram_in), .en(and_30_out), .clk(CK), .Q(high_adress_out));  // open: clr
  Register JPC (.D(ram_in), .en(and_31_out), .clk(CK), .Q(JPC_q));  // open: clr
  Register #(.width(2)) EF (.D(nand_1_out), .en(stack_out), .clk(CK), .Q(EF_q));  // open: clr
  xor xor_29 (xor_29_out, instruction[3], SP_q[0]);
  nand nand_3 (nand_3_out[0], SP_q[0], SP_q[0]);
  MUX_8_bits B_pop_A_push (.X(B_pop_A_push_x), .B(SP_q), .A(B_SP_A_ram_x), .Sel(instruction[3]));
  MUX_8_bits A_r2_B_push (.X(ram_out), .B(r2_in), .A(B_SP_MPA_A_CPC_CPA_x), .Sel(push_s_out));
  MUX_8_bits B_SP_MPA_A_CPC_CPA (.X(B_SP_MPA_A_CPC_CPA_x), .B(B_SP_A_MPA_x), .A(B_CPC_A_CPA_x), .Sel(instruction[1]));
  MUX_8_bits B_CPC_A_CPA (.X(B_CPC_A_CPA_x), .B(CPC_out), .A(CPA_out), .Sel(instruction[0]));
  MUX_8_bits B_SP_A_MPA (.X(B_SP_A_MPA_x), .B(SP_q), .A(high_adress_out), .Sel(instruction[0]));
  and and_29 (and_29_out, pop_s_out, and_52_out);
  and and_30 (and_30_out, pop_s_out, and_53_out);
  and and_31 (and_31_out, pop_s_out, and_54_out);
  and and_32 (and_32_out, pop_s_out, and_55_out);
  or or_8 (or_8_out, true_out, C_out);
  or or_9 (or_9_out, or_8_out, O_out);
  or or_10 (or_10_out, or_9_out, P_out);
  or or_11 (or_11_out, or_10_out, N_out);
  or or_12 (or_12_out, or_11_out, Z_out);
  or or_13 (or_13_out, or_12_out, E_out);
  or or_14 (or_14_out, or_13_out, F_out);
  and and_33 (and_33_out, or_14_out, jmp_out);
  MUX_8_bits B_SP_A_r1 (.X(low_adress_out), .B(r1_in), .A(B_pop_A_push_x), .Sel(stack_out));
  and and_34 (and_34_out, nand_9_out, instruction[2]);
  and push_s (push_s_out, and_34_out, stack_out);
  and and_35 (and_35_out, instruction[3], instruction[2]);
  and pop_s (pop_s_out, and_35_out, stack_out);
  and stack (stack_out, and_56_out, and_57_out);
  and and_36 (and_36_out, nand_9_out, nand_8_out);
  and true (true_out, and_36_out, and_37_out);
  and and_37 (and_37_out, nand_7_out, instruction[0]);
  and and_38 (and_38_out, nand_9_out, nand_8_out);
  and C (C_out, and_38_out, and_39_out);
  and and_39 (and_39_out, instruction[1], xor_30_out);
  and and_40 (and_40_out, nand_9_out, instruction[2]);
  and O (O_out, and_40_out, and_41_out);
  and and_41 (and_41_out, nand_7_out, xor_31_out);
  and and_42 (and_42_out, nand_9_out, instruction[2]);
  and P (P_out, and_42_out, and_43_out);
  and and_43 (and_43_out, instruction[1], xor_32_out);
  and and_44 (and_44_out, instruction[3], nand_8_out);
  and N (N_out, and_44_out, and_45_out);
  and and_45 (and_45_out, nand_7_out, xor_33_out);
  and and_46 (and_46_out, instruction[3], nand_8_out);
  and Z (Z_out, and_46_out, and_47_out);
  and and_47 (and_47_out, instruction[1], xor_34_out);
  and and_48 (and_48_out, instruction[3], instruction[2]);
  and E (E_out, and_48_out, and_49_out);
  and and_49 (and_49_out, nand_7_out, xor_35_out);
  and and_50 (and_50_out, instruction[3], instruction[2]);
  and F (F_out, and_50_out, and_51_out);
  and and_51 (and_51_out, instruction[1], xor_36_out);
  and jmp (jmp_out, and_58_out, and_59_out);
  and and_52 (and_52_out, nand_7_out, nand_6_out);
  and and_53 (and_53_out, nand_7_out, instruction[0]);
  and and_54 (and_54_out, instruction[1], nand_6_out);
  and and_55 (and_55_out, instruction[1], instruction[0]);
  and and_56 (and_56_out, nand_5_out, nand_4_out);
  and and_57 (and_57_out, nand_11_out, instruction[4]);
  xor xor_30 (xor_30_out, COPNZ_in[4], instruction[0]);
  xor xor_31 (xor_31_out, COPNZ_in[3], instruction[0]);
  xor xor_32 (xor_32_out, COPNZ_in[2], instruction[0]);
  xor xor_33 (xor_33_out, COPNZ_in[1], instruction[0]);
  xor xor_34 (xor_34_out, COPNZ_in[0], instruction[0]);
  xor xor_35 (xor_35_out, EF_q[0], instruction[0]);
  xor xor_36 (xor_36_out, EF_q[1], instruction[0]);
  and and_58 (and_58_out, nand_5_out, nand_4_out);
  and and_59 (and_59_out, nand_11_out, nand_10_out);
  nand nand_4 (nand_4_out, instruction[6], instruction[6]);
  nand nand_5 (nand_5_out, instruction[7], instruction[7]);
  nand nand_6 (nand_6_out, instruction[0], instruction[0]);
  nand nand_7 (nand_7_out, instruction[1], instruction[1]);
  nand nand_8 (nand_8_out, instruction[2], instruction[2]);
  nand nand_9 (nand_9_out, instruction[3], instruction[3]);
  nand nand_10 (nand_10_out, instruction[4], instruction[4]);
  nand nand_11 (nand_11_out, instruction[5], instruction[5]);
endmodule

module tests_unites (
  input  [7:0] input_1,
  input  [7:0] instruction,
  input  [7:0] ram_in,
  output [7:0] output_1,
  output \end ,
  output [7:0] r2,
  output [7:0] ram_out,
  output [7:0] r1,
  output [7:0] low_adress,
  output [4:0] COPNZ,
  output [7:0] high_adress,
  output [7:0] CPA,
  output [7:0] CPC
);

  wire CK_1_out, CK_2_out;

  Clock CK_2 (.out(CK_2_out));
  UCP ucp_1 (
    .ram_out(ram_out), .CPC_out(CPC), .CPA_out(CPA), .high_adress_out(high_adress),
    .low_adress_out(low_adress), .end_out(\end ), .CK(CK_2_out), .r2_in(r2), .ram_in(ram_in), .r1_in(r1),
    .instruction(instruction), .COPNZ_in(COPNZ));
  Clock CK_1 (.out(CK_1_out));
  UAL ual_1 (
    .OUT_out(output_1), .COPNZ_out(COPNZ), .r1_out(r1), .r2_out(r2), .CK(CK_1_out), .ram_in(ram_in),
    .IN_in(input_1), .instruction(instruction));
endmodule

module UCK (
  input  start_in,
  input  end_in,
  input  CK_in,
  output LED_out,
  output CK_out
);

  xor xor_1 (LED_out, start_in, end_in);
  and and_1 (CK_out, LED_out, CK_in);
endmodule

module UCM (
  input  [7:0] instruction,
  output write_out,
  output read_out
);

  wire and_2_out, and_3_out, nand_1_out, nand_2_out, nand_3_out, nand_4_out;

  and and_1 (write_out, and_2_out, nand_4_out);
  and and_2 (and_2_out, and_3_out, instruction[4]);
  nand nand_1 (nand_1_out, instruction[7], instruction[7]);
  and and_3 (and_3_out, nand_1_out, nand_2_out);
  nand nand_2 (nand_2_out, instruction[6], instruction[6]);
  nand nand_3 (nand_3_out, instruction[5], instruction[5]);
  nand nand_4 (nand_4_out, nand_3_out, instruction[3]);

  assign read_out = 1'b1;
endmodule

// MUX
module MUX_8_bits (
  input  [7:0] B,
  input  [7:0] A,
  input  Sel,
  output [7:0] X
);

  wire nand_1_out, nand_2_out, nand_3_out, nand_5_out, nand_6_out, nand_8_out, nand_9_out, nand_11_out,
       nand_12_out, nand_14_out, nand_15_out, nand_17_out, nand_18_out, nand_20_out, nand_21_out,
       nand_23_out, nand_24_out;

  nand nand_1 (nand_1_out, nand_23_out, B[7]);
  nand nand_2 (nand_2_out, Sel, A[7]);
  nand nand_3 (nand_3_out, nand_23_out, B[6]);
  nand nand_4 (X[7], nand_1_out, nand_2_out);
  nand nand_5 (nand_5_out, Sel, A[6]);
  nand nand_6 (nand_6_out, nand_23_out, B[5]);
  nand nand_7 (X[6], nand_3_out, nand_5_out);
  nand nand_8 (nand_8_out, Sel, A[5]);
  nand nand_9 (nand_9_out, nand_23_out, B[4]);
  nand nand_10 (X[5], nand_6_out, nand_8_out);
  nand nand_11 (nand_11_out, Sel, A[4]);
  nand nand_12 (nand_12_out, nand_23_out, B[3]);
  nand nand_13 (X[4], nand_9_out, nand_11_out);
  nand nand_14 (nand_14_out, Sel, A[3]);
  nand nand_15 (nand_15_out, nand_23_out, B[2]);
  nand nand_16 (X[3], nand_12_out, nand_14_out);
  nand nand_17 (nand_17_out, Sel, A[2]);
  nand nand_18 (nand_18_out, nand_23_out, B[1]);
  nand nand_19 (X[2], nand_15_out, nand_17_out);
  nand nand_20 (nand_20_out, Sel, A[1]);
  nand nand_21 (nand_21_out, nand_23_out, B[0]);
  nand nand_22 (X[1], nand_18_out, nand_20_out);
  nand nand_23 (nand_23_out, Sel, Sel);
  nand nand_24 (nand_24_out, Sel, A[0]);
  nand nand_25 (X[0], nand_21_out, nand_24_out);
endmodule
